# Fritzing sketch usb-cable-load (saved by Fritzing 0.9.2b)
circuit board: 5.12796cm x 6.56788cm
breadboards: 1

parts:
  USB_B = USB+SHIELD [package=usb-b-pth]
  D4 = Schottky Diode [part_number=1N5817 package="300 mil [THT]"]
  D3 = Schottky Diode [part_number=1N5817 package="300 mil [THT]"]
  D1 = Schottky Diode [part_number=1N5817 package="300 mil [THT]"]
  miniUSB = Mini-USB _B_ connector with 5th pin broken out. [package=usb-minib]
  microUSB = USB_AB [package=usb-ab-micro-smd]
  D2 = Schottky Diode [part_number=1N5817 package="300 mil [THT]"]
  USB_A = USB Connectors [package=usb-a-h]
  R1 = 10W Resistor [package=THT]

nets:
  GND: USB_B.P$1, USB_B.P$2, USB_B.GND, miniUSB.MTN2, miniUSB.MTN3, miniUSB.MTN1, miniUSB.MTN4, miniUSB.GND, microUSB.GND, USB_A.GND, R1.Pin_1
  N1: USB_B.VBUS, D4.anode
  N2: D4.cathode, D3.cathode, D1.cathode, D2.cathode, R1.Pin_0
  N3: D3.anode, USB_A.VBUS
  N4: D1.anode, miniUSB.VBUS
  N5: microUSB.VBUS, D2.anode

custom parts:
  10W Resistor: Cement resistor (10W)
